// Logisim project Lab4.circ as structural Verilog: 8 circuits, main circuit main
module main (
  input  Reset,
  output [31:0] out_2
);

  wire ALUSrc, and_1_out, Branch, clock_1_out, MemRead, MemtoReg, MemWrite, RegDest, RegWrite, Zero;
  wire [1:0] AluOp;
  wire [2:0] alucontrol_1_opcode;
  wire [4:0] multiplexer_1_out, separadorbits_1_rd, separadorbits_1_rs, separadorbits_1_rt;
  wire [5:0] separadorbits_1_funtion, separadorbits_1_op_code;
  wire [15:0] separadorbits_1_inmediate;
  wire [31:0] adder_1_out, adder_3_out, alu_1_resultado, bancoregistros_1_read_data_1,
       bancoregistros_1_read_data_2, Extension_signo, memoria_1_read_2, multiplexer_2_out, multiplexer_3_out,
       R_ALu, register_1_q;

  Clock clock_1 (.out(clock_1_out));
  Register #(.width(32)) register_1 (
    .D(multiplexer_3_out), .Q(register_1_q), .clk(clock_1_out), .clr(Reset));  // open: en
  MemoriaInstrucciones memoriainstrucciones_1 (
    .Adress(register_1_q), .Clock(clock_1_out), .Reset(Reset), .Instruccion(out_2));
  Adder #(.width(32)) adder_1 (.a(32'h1), .b(register_1_q), .out(adder_1_out));  // open: cin, cout
  Control control_1 (
    .OpCode5(separadorbits_1_op_code[5]), .OpCode4(separadorbits_1_op_code[4]),
    .OpCode3(separadorbits_1_op_code[3]), .OpCode2(separadorbits_1_op_code[2]),
    .OpCode1(separadorbits_1_op_code[1]), .OpCode0(separadorbits_1_op_code[0]), .RegDest(RegDest),
    .Branch(Branch), .MemRead(MemRead), .MemtoReg(MemtoReg), .ALUOp(AluOp), .MemWrite(MemWrite),
    .ALUSrc(ALUSrc), .RegWrite(RegWrite));
  SeparadorBits separadorbits_1 (
    .in_1(out_2), .Op_Code(separadorbits_1_op_code), .rs(separadorbits_1_rs), .rt(separadorbits_1_rt),
    .rd(separadorbits_1_rd), .funtion(separadorbits_1_funtion), .Inmediate(separadorbits_1_inmediate));  // open: shamt, Adress
  Multiplexer #(.width(5), .enable("false")) multiplexer_1 (
    .in0(separadorbits_1_rt), .in1(separadorbits_1_rd), .out(multiplexer_1_out), .sel(RegDest));
  assign Extension_signo = {{16{1'b0}}, separadorbits_1_inmediate};  // Bit_Extender bit_extender_1
  Adder #(.width(32)) adder_2 (.b(32'h1));  // open: a, out, cin, cout
  BancoRegistros bancoregistros_1 (
    .Read_Register_1(separadorbits_1_rs), .Read_Register_2(separadorbits_1_rt), .Clock(clock_1_out),
    .reset(Reset), .Write_Register(multiplexer_1_out), .Write(RegWrite),
    .Read_Data_1(bancoregistros_1_read_data_1), .Read_Data_2(bancoregistros_1_read_data_2), .Write_Data(R_ALu));
  Adder #(.width(32)) adder_3 (.a(adder_1_out), .b(Extension_signo), .out(adder_3_out));  // open: cin, cout
  and and_1 (and_1_out, Branch, Zero);
  Multiplexer #(.width(32), .enable("false")) multiplexer_2 (
    .in0(bancoregistros_1_read_data_2), .in1(Extension_signo), .out(multiplexer_2_out), .sel(ALUSrc));
  Multiplexer #(.width(32), .enable("false")) multiplexer_3 (
    .in0(adder_1_out), .in1(adder_3_out), .out(multiplexer_3_out), .sel(and_1_out));
  ALUControl alucontrol_1 (.AluOp(AluOp), .Function(separadorbits_1_funtion), .OpCode(alucontrol_1_opcode));
  ALU alu_1 (
    .Data_1(bancoregistros_1_read_data_1), .Data_2(multiplexer_2_out), .OpCode(alucontrol_1_opcode),
    .Resultado(alu_1_resultado), .Zero(Zero));
  Memoria memoria_1 (
    .Adress(alu_1_resultado), .Write(bancoregistros_1_read_data_2), .Read_2(memoria_1_read_2),
    .Clock(clock_1_out), .Read(MemRead), .Write_2(MemWrite), .Reset(Reset));
  Multiplexer #(.width(32), .enable("false")) multiplexer_4 (
    .in0(alu_1_resultado), .in1(memoria_1_read_2), .out(R_ALu), .sel(MemtoReg));

  // Notes on the sheet:
  //   PC
  //   Instrucciones
  //   Control
  //   Banco
  //   AluControl
  //   ALU
  //   Memoria de Datos
endmodule

module SeparadorBits (
  input  [31:0] in_1,
  output [5:0] Op_Code,
  output [4:0] rs,
  output [4:0] rt,
  output [4:0] rd,
  output [4:0] shamt,
  output [5:0] funtion,
  output [15:0] Inmediate,
  output [25:0] Adress
);


  assign Adress = in_1[25:0];
  assign funtion = in_1[5:0];
  assign Inmediate = in_1[15:0];
  assign Op_Code = in_1[31:26];
  assign rd = in_1[15:11];
  assign rs = in_1[25:21];
  assign rt = in_1[20:16];
  assign shamt = in_1[10:6];
endmodule

module ALUControl (
  input  [1:0] AluOp,
  input  [5:0] Function,
  output [2:0] OpCode
);

  wire and_1_out, and_2_out, and_3_out, and_4_out, and_5_out, and_6_out, and_7_out, and_8_out, and_9_out,
       not_1_out, not_2_out, not_3_out, not_4_out, not_5_out, not_6_out, not_7_out, not_8_out, not_9_out,
       not_10_out, not_11_out, not_12_out, not_13_out, not_14_out, not_15_out, not_16_out, not_17_out,
       not_18_out, not_19_out, not_20_out, not_21_out, not_22_out, not_23_out, not_24_out, not_25_out,
       not_26_out, not_27_out, not_28_out, not_29_out, not_30_out, not_31_out, not_32_out, not_33_out,
       not_34_out;

  not not_1 (not_1_out, AluOp[0]);
  not not_2 (not_2_out, Function[4]);
  not not_3 (not_3_out, Function[2]);
  not not_4 (not_4_out, Function[0]);
  not not_5 (not_5_out, AluOp[0]);
  not not_6 (not_6_out, Function[4]);
  not not_7 (not_7_out, Function[3]);
  not not_8 (not_8_out, Function[1]);
  not not_9 (not_9_out, Function[0]);
  not not_10 (not_10_out, AluOp[0]);
  not not_11 (not_11_out, AluOp[1]);
  not not_12 (not_12_out, AluOp[0]);
  not not_13 (not_13_out, Function[4]);
  not not_14 (not_14_out, Function[3]);
  not not_15 (not_15_out, Function[2]);
  not not_16 (not_16_out, Function[1]);
  not not_17 (not_17_out, Function[0]);
  not not_18 (not_18_out, AluOp[1]);
  not not_19 (not_19_out, AluOp[0]);
  not not_20 (not_20_out, Function[4]);
  not not_21 (not_21_out, Function[3]);
  not not_22 (not_22_out, AluOp[0]);
  not not_23 (not_23_out, Function[5]);
  not not_24 (not_24_out, Function[2]);
  not not_25 (not_25_out, Function[0]);
  not not_26 (not_26_out, AluOp[0]);
  not not_27 (not_27_out, Function[4]);
  not not_28 (not_28_out, Function[3]);
  not not_29 (not_29_out, Function[2]);
  not not_30 (not_30_out, Function[0]);
  not not_31 (not_31_out, AluOp[0]);
  not not_32 (not_32_out, Function[4]);
  not not_33 (not_33_out, Function[2]);
  not not_34 (not_34_out, Function[0]);
  and and_1 (and_1_out, not_1_out, Function[5], not_2_out, not_3_out, Function[1], not_4_out);
  and and_2 (and_2_out, not_5_out, Function[5], not_6_out, not_7_out, Function[2], not_8_out, not_9_out);
  and and_3 (and_3_out, AluOp[1], not_10_out);
  and and_4 (and_4_out, not_11_out, not_12_out, Function[5], not_13_out, not_14_out, not_15_out, not_16_out, not_17_out);
  and and_5 (and_5_out, not_18_out, not_19_out, Function[5], not_20_out, not_21_out, Function[2], Function[0]);
  and and_6 (and_6_out, AluOp[1], AluOp[0]);
  and and_7 (and_7_out, not_22_out, not_23_out, Function[4], Function[3], not_24_out, Function[1], not_25_out);
  and and_8 (and_8_out, not_26_out, Function[5], not_27_out, not_28_out, not_29_out, not_30_out);
  and and_9 (and_9_out, not_31_out, Function[5], not_32_out, not_33_out, Function[1], not_34_out);
  or or_1 (OpCode[2], and_1_out, and_2_out, and_3_out);
  or or_2 (OpCode[1], and_4_out, and_5_out, and_6_out);
  or or_3 (OpCode[0], and_7_out, and_8_out, and_9_out, AluOp[1]);
endmodule

module BancoRegistros (
  input  [4:0] Read_Register_1,
  input  [4:0] Read_Register_2,
  input  Clock,
  input  reset,
  input  [31:0] Write_Data,
  input  [4:0] Write_Register,
  input  Write,
  output [31:0] Read_Data_1,
  output [31:0] Read_Data_2
);

  wire decoder_1_out1, decoder_1_out2, decoder_1_out3, decoder_1_out4, decoder_1_out5, decoder_1_out6,
       decoder_1_out7, decoder_1_out8, decoder_1_out9, decoder_1_out10, decoder_1_out11, decoder_1_out12,
       decoder_1_out13, decoder_1_out14, decoder_1_out15, decoder_1_out16, decoder_1_out17, decoder_1_out18,
       decoder_1_out19, decoder_1_out20, decoder_1_out21, decoder_1_out22, decoder_1_out23, decoder_1_out24,
       decoder_1_out25, decoder_1_out26, decoder_1_out27, decoder_1_out28, decoder_1_out29, decoder_1_out30,
       decoder_1_out31;
  wire [31:0] a0_q, a1_q, a2_q, a3_q, at_q, fp_q, gp_q, k0_q, k1_q, ra_q, s0_q, s1_q, s2_q, s3_q, s4_q, s5_q,
       s6_q, s7_q, sp_q, t0_q, t1_q, t2_q, t3_q, t4_q, t5_q, t6_q, t7_q, t8_q, t9_q, v0_q, v1_q;

  Decoder #(.select(5), .disabled(0)) decoder_1 (
    .out1(decoder_1_out1), .out2(decoder_1_out2), .out3(decoder_1_out3), .out4(decoder_1_out4),
    .out5(decoder_1_out5), .out6(decoder_1_out6), .out7(decoder_1_out7), .out8(decoder_1_out8),
    .out9(decoder_1_out9), .out10(decoder_1_out10), .out11(decoder_1_out11), .out12(decoder_1_out12),
    .out13(decoder_1_out13), .out14(decoder_1_out14), .out15(decoder_1_out15), .out16(decoder_1_out16),
    .out17(decoder_1_out17), .out18(decoder_1_out18), .out19(decoder_1_out19), .out20(decoder_1_out20),
    .out21(decoder_1_out21), .out22(decoder_1_out22), .out23(decoder_1_out23), .out24(decoder_1_out24),
    .out25(decoder_1_out25), .out26(decoder_1_out26), .out27(decoder_1_out27), .out28(decoder_1_out28),
    .out29(decoder_1_out29), .out30(decoder_1_out30), .out31(decoder_1_out31), .sel(Write_Register),
    .en(Write));  // open: out0
  Register #(.width(32)) at (.D(Write_Data), .en(decoder_1_out1), .Q(at_q), .clk(Clock), .clr(reset));
  Register #(.width(32)) v0 (.D(Write_Data), .en(decoder_1_out2), .Q(v0_q), .clk(Clock), .clr(reset));
  Register #(.width(32)) v1 (.D(Write_Data), .en(decoder_1_out3), .Q(v1_q), .clk(Clock), .clr(reset));
  Register #(.width(32)) a0 (.D(Write_Data), .en(decoder_1_out4), .Q(a0_q), .clk(Clock), .clr(reset));
  Register #(.width(32)) a1 (.D(Write_Data), .en(decoder_1_out5), .Q(a1_q), .clk(Clock), .clr(reset));
  Register #(.width(32)) a2 (.D(Write_Data), .en(decoder_1_out6), .Q(a2_q), .clk(Clock), .clr(reset));
  Register #(.width(32)) a3 (.D(Write_Data), .en(decoder_1_out7), .Q(a3_q), .clk(Clock), .clr(reset));
  Register #(.width(32)) t0 (.D(Write_Data), .en(decoder_1_out8), .Q(t0_q), .clk(Clock), .clr(reset));
  Register #(.width(32)) t1 (.D(Write_Data), .en(decoder_1_out9), .Q(t1_q), .clk(Clock), .clr(reset));
  Register #(.width(32)) t2 (.D(Write_Data), .en(decoder_1_out10), .Q(t2_q), .clk(Clock), .clr(reset));
  Register #(.width(32)) t3 (.D(Write_Data), .en(decoder_1_out11), .Q(t3_q), .clk(Clock), .clr(reset));
  Register #(.width(32)) t4 (.D(Write_Data), .en(decoder_1_out12), .Q(t4_q), .clk(Clock), .clr(reset));
  Register #(.width(32)) t5 (.D(Write_Data), .en(decoder_1_out13), .Q(t5_q), .clk(Clock), .clr(reset));
  Register #(.width(32)) t6 (.D(Write_Data), .en(decoder_1_out14), .Q(t6_q), .clk(Clock), .clr(reset));
  Register #(.width(32)) t7 (.D(Write_Data), .en(decoder_1_out15), .Q(t7_q), .clk(Clock), .clr(reset));
  Register #(.width(32)) s0 (.D(Write_Data), .en(decoder_1_out16), .Q(s0_q), .clk(Clock), .clr(reset));
  Register #(.width(32)) s1 (.D(Write_Data), .en(decoder_1_out17), .Q(s1_q), .clk(Clock), .clr(reset));
  Register #(.width(32)) s2 (.D(Write_Data), .en(decoder_1_out18), .Q(s2_q), .clk(Clock), .clr(reset));
  Register #(.width(32)) s3 (.D(Write_Data), .en(decoder_1_out19), .Q(s3_q), .clk(Clock), .clr(reset));
  Register #(.width(32)) s4 (.D(Write_Data), .en(decoder_1_out20), .Q(s4_q), .clk(Clock), .clr(reset));
  Register #(.width(32)) s5 (.D(Write_Data), .en(decoder_1_out21), .Q(s5_q), .clk(Clock), .clr(reset));
  Register #(.width(32)) s6 (.D(Write_Data), .en(decoder_1_out22), .Q(s6_q), .clk(Clock), .clr(reset));
  Register #(.width(32)) s7 (.D(Write_Data), .en(decoder_1_out23), .Q(s7_q), .clk(Clock), .clr(reset));
  Register #(.width(32)) t8 (.D(Write_Data), .en(decoder_1_out24), .Q(t8_q), .clk(Clock), .clr(reset));
  Register #(.width(32)) t9 (.D(Write_Data), .en(decoder_1_out25), .Q(t9_q), .clk(Clock), .clr(reset));
  Register #(.width(32)) k0 (.D(Write_Data), .en(decoder_1_out26), .Q(k0_q), .clk(Clock), .clr(reset));
  Register #(.width(32)) k1 (.D(Write_Data), .en(decoder_1_out27), .Q(k1_q), .clk(Clock), .clr(reset));
  Register #(.width(32)) gp (.D(Write_Data), .en(decoder_1_out28), .Q(gp_q), .clk(Clock), .clr(reset));
  Register #(.width(32)) sp (.D(Write_Data), .en(decoder_1_out29), .Q(sp_q), .clk(Clock), .clr(reset));
  Register #(.width(32)) fp (.D(Write_Data), .en(decoder_1_out30), .Q(fp_q), .clk(Clock), .clr(reset));
  Register #(.width(32)) ra (.D(Write_Data), .en(decoder_1_out31), .Q(ra_q), .clk(Clock), .clr(reset));
  Multiplexer #(.select(5), .width(32), .enable("false")) multiplexer_1 (
    .in0({32{1'b0}}), .in1(at_q), .in2(v0_q), .in3(v1_q), .in4(a0_q), .in5(a1_q), .in6(a2_q), .in7(a3_q),
    .in8(t0_q), .in9(t1_q), .in10(t2_q), .in11(t3_q), .in12(t4_q), .in13(t5_q), .in14(t6_q), .in15(t7_q),
    .in16(s0_q), .in17(s1_q), .in18(s2_q), .in19(s3_q), .in20(s4_q), .in21(s5_q), .in22(s6_q), .in23(s7_q),
    .in24(t8_q), .in25(t9_q), .in26(k0_q), .in27(k1_q), .in28(gp_q), .in29(sp_q), .in30(fp_q), .in31(ra_q),
    .out(Read_Data_1), .sel(Read_Register_1));
  Multiplexer #(.select(5), .width(32), .enable("false")) multiplexer_2 (
    .in0({32{1'b0}}), .in1(at_q), .in2(v0_q), .in3(v1_q), .in4(a0_q), .in5(a1_q), .in6(a2_q), .in7(a3_q),
    .in8(t0_q), .in9(t1_q), .in10(t2_q), .in11(t3_q), .in12(t4_q), .in13(t5_q), .in14(t6_q), .in15(t7_q),
    .in16(s0_q), .in17(s1_q), .in18(s2_q), .in19(s3_q), .in20(s4_q), .in21(s5_q), .in22(s6_q), .in23(s7_q),
    .in24(t8_q), .in25(t9_q), .in26(k0_q), .in27(k1_q), .in28(gp_q), .in29(sp_q), .in30(fp_q), .in31(ra_q),
    .out(Read_Data_2), .sel(Read_Register_2));

  // Other names for the same wires on the sheet: Read_R1[4:0] = Read_Register_1; Read_R2[4:0] = Read_Register_2

  // Notes on the sheet:
  //   $Zero
endmodule

module ALU (
  input  [31:0] Data_1,
  input  [31:0] Data_2,
  input  [2:0] OpCode,
  output [31:0] Resultado,
  output Zero
);

  wire comparator_1_lt;
  wire [31:0] adder_1_out, and_1_out, bit_extender_1_out, divider_1_out, nor_1_out, or_1_out,
       subtractor_1_out;

  Comparator #(.width(32)) comparator_1 (.a(Data_1), .b(Data_2), .lt(comparator_1_lt));  // open: gt, eq
  assign nor_1_out = ~(Data_1 | Data_2);  // NOR_Gate nor_1, 32 bits wide
  Divider #(.width(32)) divider_1 (.a(Data_1), .b(Data_2), .out(divider_1_out));  // open: upper, rem
  assign or_1_out = Data_1 | Data_2;  // OR_Gate or_1, 32 bits wide
  Adder #(.width(32)) adder_1 (.a(Data_1), .b(Data_2), .out(adder_1_out));  // open: cin, cout
  Subtractor #(.width(32)) subtractor_1 (.a(Data_1), .b(Data_2), .out(subtractor_1_out));  // open: bin, bout
  assign and_1_out = Data_1 & Data_2;  // AND_Gate and_1, 32 bits wide
  assign bit_extender_1_out = {{31{1'b0}}, comparator_1_lt};  // Bit_Extender bit_extender_1
  Multiplexer #(.select(3), .width(32), .enable("false")) multiplexer_1 (
    .in0({32{1'b0}}), .in1(divider_1_out), .in2(or_1_out), .in3(adder_1_out), .in4(and_1_out),
    .in5(subtractor_1_out), .in6(bit_extender_1_out), .in7(nor_1_out), .out(Resultado), .sel(OpCode));
  Comparator #(.width(32)) comparator_2 (.a(subtractor_1_out), .b({32{1'b0}}), .eq(Zero));  // open: gt, lt

  // Notes on the sheet:
  //   S
  //   R
  //   Add - 3 - 011
  //   Sub - 5 - 101
  //   And - 4 - 100
  //   Or - 2 - 010
  //   Nor - 7 - 111
  //   SLT - 6 - 110
  //   Div - 1 - 001
endmodule

module Control (
  input  OpCode5,
  input  OpCode4,
  input  OpCode3,
  input  OpCode2,
  input  OpCode1,
  input  OpCode0,
  output RegDest,
  output Branch,
  output MemRead,
  output MemtoReg,
  output [1:0] ALUOp,
  output MemWrite,
  output ALUSrc,
  output RegWrite
);

  wire and_5_out, and_6_out, and_7_out, and_8_out, and_9_out, and_11_out, and_12_out, and_13_out, and_14_out,
       not_1_out, not_2_out, not_3_out, not_4_out, not_5_out, not_6_out, not_7_out, not_8_out, not_9_out,
       not_10_out, not_11_out, not_12_out, not_13_out, not_14_out, not_15_out, not_16_out, not_17_out,
       not_18_out, not_19_out, not_20_out, not_21_out, not_22_out, not_23_out, not_24_out, not_25_out,
       not_26_out, not_27_out, not_28_out, not_29_out, not_30_out, not_31_out, not_32_out, not_33_out,
       not_34_out, not_35_out, not_36_out, not_37_out, not_38_out, not_39_out, not_40_out, not_41_out,
       not_42_out, not_43_out, not_44_out, not_45_out, not_46_out, not_47_out, not_48_out, not_49_out,
       not_50_out, not_51_out, not_52_out, not_53_out;

  not not_1 (not_1_out, OpCode5);
  not not_2 (not_2_out, OpCode4);
  not not_3 (not_3_out, OpCode3);
  not not_4 (not_4_out, OpCode2);
  not not_5 (not_5_out, OpCode1);
  not not_6 (not_6_out, OpCode0);
  not not_7 (not_7_out, OpCode5);
  not not_8 (not_8_out, OpCode4);
  not not_9 (not_9_out, OpCode3);
  not not_10 (not_10_out, OpCode1);
  not not_11 (not_11_out, OpCode0);
  not not_12 (not_12_out, OpCode4);
  not not_13 (not_13_out, OpCode3);
  not not_14 (not_14_out, OpCode2);
  not not_15 (not_15_out, OpCode4);
  not not_16 (not_16_out, OpCode3);
  not not_17 (not_17_out, OpCode2);
  not not_18 (not_18_out, OpCode5);
  not not_19 (not_19_out, OpCode4);
  not not_20 (not_20_out, OpCode3);
  not not_21 (not_21_out, OpCode1);
  not not_22 (not_22_out, OpCode0);
  not not_23 (not_23_out, OpCode5);
  not not_24 (not_24_out, OpCode4);
  not not_25 (not_25_out, OpCode2);
  not not_26 (not_26_out, OpCode1);
  not not_27 (not_27_out, OpCode0);
  not not_28 (not_28_out, OpCode4);
  not not_29 (not_29_out, OpCode2);
  not not_30 (not_30_out, OpCode5);
  not not_31 (not_31_out, OpCode4);
  not not_32 (not_32_out, OpCode2);
  not not_33 (not_33_out, OpCode1);
  not not_34 (not_34_out, OpCode0);
  not not_35 (not_35_out, OpCode4);
  not not_36 (not_36_out, OpCode2);
  not not_37 (not_37_out, OpCode4);
  not not_38 (not_38_out, OpCode2);
  not not_39 (not_39_out, OpCode5);
  not not_40 (not_40_out, OpCode4);
  not not_41 (not_41_out, OpCode2);
  not not_42 (not_42_out, OpCode1);
  not not_43 (not_43_out, OpCode0);
  not not_44 (not_44_out, OpCode4);
  not not_45 (not_45_out, OpCode2);
  not not_46 (not_46_out, OpCode5);
  not not_47 (not_47_out, OpCode4);
  not not_48 (not_48_out, OpCode2);
  not not_49 (not_49_out, OpCode1);
  not not_50 (not_50_out, OpCode0);
  not not_51 (not_51_out, OpCode4);
  not not_52 (not_52_out, OpCode3);
  not not_53 (not_53_out, OpCode2);
  and and_1 (RegDest, not_1_out, not_2_out, not_3_out, not_4_out, not_5_out, not_6_out);
  and and_2 (Branch, not_7_out, not_8_out, not_9_out, OpCode2, not_10_out, not_11_out);
  and and_3 (MemRead, OpCode5, not_12_out, not_13_out, not_14_out, OpCode1, OpCode0);
  and and_4 (MemtoReg, OpCode5, not_15_out, not_16_out, not_17_out, OpCode1, OpCode0);
  and and_5 (and_5_out, not_18_out, not_19_out, not_20_out, OpCode2, not_21_out, not_22_out);
  and and_6 (and_6_out, not_23_out, not_24_out, OpCode3, not_25_out, not_26_out, not_27_out);
  and and_7 (and_7_out, OpCode5, not_28_out, not_29_out, OpCode1, OpCode0);
  and and_8 (and_8_out, not_30_out, not_31_out, OpCode3, not_32_out, not_33_out, not_34_out);
  and and_9 (and_9_out, OpCode5, not_35_out, not_36_out, OpCode1, OpCode0);
  and and_10 (MemWrite, OpCode5, not_37_out, OpCode3, not_38_out, OpCode1, OpCode0);
  and and_11 (and_11_out, not_39_out, not_40_out, OpCode3, not_41_out, not_42_out, not_43_out);
  and and_12 (and_12_out, OpCode5, not_44_out, not_45_out, OpCode1, OpCode0);
  and and_13 (and_13_out, not_46_out, not_47_out, not_48_out, not_49_out, not_50_out);
  and and_14 (and_14_out, OpCode5, not_51_out, not_52_out, not_53_out, OpCode1, OpCode0);
  or or_1 (ALUOp[1], and_5_out, and_6_out, and_7_out);
  or or_2 (ALUOp[0], and_8_out, and_9_out);
  or or_3 (ALUSrc, and_11_out, and_12_out);
  or or_4 (RegWrite, and_13_out, and_14_out);

  // Notes on the sheet:
  //   R 00
  //   SW/LW 01
  //   BEQ 11
endmodule

module Memoria (
  input  [31:0] Adress,
  input  [31:0] Write,
  input  Write_2,
  input  Clock,
  input  Read,
  input  Reset,
  output [31:0] Read_2
);

  RAM #(.addrWidth(10), .dataWidth(32), .bus("separate")) ram_1 (
    .addr(Adress[9:0]), .din(Write), .data(Read_2), .str(Write_2), .clk(Clock), .ld(Read), .clr(Reset));  // open: sel
endmodule

module MemoriaInstrucciones (
  input  [31:0] Adress,
  input  Clock,
  input  Reset,
  output [31:0] Instruccion
);

  RAM #(.addrWidth(10), .dataWidth(32), .bus("separate")) ram_1 (
    .addr(Adress[9:0]), .data(Instruccion), .clk(Clock), .clr(Reset));  // open: din, str, sel, ld
endmodule
